// Logisim project control-logic.circ as structural Verilog: 1 circuit, main circuit control_logic
module control_logic (
  input  [31:0] Instruction,
  input  BrEq,
  input  BrLt,
  output PCSel,
  output RegWEn,
  output [2:0] ImmSel,
  output BrUn,
  output ASel,
  output BSel,
  output [3:0] ALUSel,
  output MemWEn,
  output [1:0] WBSel
);

  wire comparator_1_eq, comparator_2_eq, comparator_3_eq, comparator_4_eq, comparator_5_eq, comparator_6_eq,
       comparator_7_eq, comparator_8_eq, comparator_9_eq, comparator_12_eq, comparator_13_eq,
       comparator_14_eq, comparator_15_eq, comparator_16_eq, comparator_17_eq, comparator_18_eq,
       comparator_19_eq, comparator_20_eq, comparator_21_eq, comparator_22_eq, comparator_23_eq,
       comparator_24_eq, comparator_25_eq, comparator_26_eq, comparator_27_eq, comparator_28_eq,
       comparator_29_eq, comparator_30_eq, comparator_31_eq, is_add, is_addi, is_and, is_andi, is_Itype,
       is_mul, is_mulh, is_mulhu, is_or, is_ori, is_Rtype, is_sll, is_slli, is_slt, is_slti, is_sra, is_srai,
       is_srl, is_srli, is_sub, is_xor, is_xori;
  wire [5:0] rom_input;
  wire [15:14] rom_1_data;

  Comparator #(.width(3)) comparator_1 (.a(Instruction[14:12]), .b(3'b000), .eq(comparator_1_eq));  // open: gt, lt
  Comparator #(.width(3)) comparator_2 (.a(Instruction[14:12]), .b(3'b001), .eq(comparator_2_eq));  // open: gt, lt
  Comparator #(.width(3)) comparator_3 (.a(Instruction[14:12]), .b(3'b010), .eq(comparator_3_eq));  // open: gt, lt
  Comparator #(.width(3)) comparator_4 (.a(Instruction[14:12]), .b(3'b100), .eq(comparator_4_eq));  // open: gt, lt
  Comparator #(.width(3)) comparator_5 (.a(Instruction[14:12]), .b(3'b101), .eq(comparator_5_eq));  // open: gt, lt
  Comparator #(.width(3)) comparator_6 (.a(Instruction[14:12]), .b(3'b110), .eq(comparator_6_eq));  // open: gt, lt
  Comparator #(.width(3)) comparator_7 (.a(Instruction[14:12]), .b(3'b111), .eq(comparator_7_eq));  // open: gt, lt
  ROM #(.addrWidth(6), .dataWidth(16)) rom_1 (
    .addr(rom_input), .data({rom_1_data, WBSel, MemWEn, ALUSel, BSel, ASel, BrUn, ImmSel, RegWEn}));
  and and_1 (is_addi, is_Itype, comparator_1_eq);
  and and_2 (is_slli, is_Itype, comparator_2_eq);
  and and_3 (is_slti, is_Itype, comparator_3_eq);
  and and_4 (is_xori, is_Itype, comparator_4_eq);
  and and_5 (is_ori, is_Itype, comparator_6_eq);
  and and_6 (is_andi, is_Itype, comparator_7_eq);
  Comparator #(.width(7)) comparator_8 (.a(Instruction[31:25]), .b({7{1'b0}}), .eq(comparator_8_eq));  // open: gt, lt
  Comparator #(.width(7)) comparator_9 (.a(7'b0100000), .b(Instruction[31:25]), .eq(comparator_9_eq));  // open: gt, lt
  and and_7 (is_srli, comparator_5_eq, is_Itype, comparator_8_eq);
  and and_8 (is_srai, comparator_5_eq, comparator_9_eq);
  Priority_Encoder #(.select_enc(6)) priority_encoder_1 (
    .in0(is_add), .in1(is_mul), .in2(is_sub), .in3(is_sll), .in4(is_mulh), .in5(is_mulhu), .in6(is_slt),
    .in7(is_xor), .in8(is_srl), .in9(is_sra), .in10(is_or), .in11(is_and), .in15(is_addi), .in16(is_slli),
    .in17(is_slti), .in18(is_xori), .in19(is_srli), .in20(is_srai), .in21(is_ori), .in22(is_andi),
    .out(rom_input));  // open: in12, in13, in14, in23, in24, in25, in26, in27, in28, in29, in30, in31, in32, in33, in34, in35, in36, in37, in38, in39, in40, in41, in42, in43, in44, in45, in46, in47, in48, in49, in50, in51, in52, in53, in54, in55, in56, in57, in58, in59, in60, in61, in62, in63, gs, en_out, en_in
  Comparator #(.width(7)) comparator_10 (.a(Instruction[6:0]), .b(7'b0110011), .eq(is_Rtype));  // open: gt, lt
  Comparator #(.width(7)) comparator_11 (.a(Instruction[6:0]), .b(7'b0010011), .eq(is_Itype));  // open: gt, lt
  Comparator #(.width(3)) comparator_12 (.a(Instruction[14:12]), .b(3'b110), .eq(comparator_12_eq));  // open: gt, lt
  Comparator #(.width(3)) comparator_13 (.a(Instruction[14:12]), .b(3'b111), .eq(comparator_13_eq));  // open: gt, lt
  Comparator #(.width(3)) comparator_14 (.a(Instruction[14:12]), .b(3'b000), .eq(comparator_14_eq));  // open: gt, lt
  Comparator #(.width(3)) comparator_15 (.a(Instruction[14:12]), .b(3'b001), .eq(comparator_15_eq));  // open: gt, lt
  Comparator #(.width(3)) comparator_16 (.a(Instruction[14:12]), .b(3'b011), .eq(comparator_16_eq));  // open: gt, lt
  Comparator #(.width(3)) comparator_17 (.a(Instruction[14:12]), .b(3'b010), .eq(comparator_17_eq));  // open: gt, lt
  Comparator #(.width(3)) comparator_18 (.a(Instruction[14:12]), .b(3'b100), .eq(comparator_18_eq));  // open: gt, lt
  Comparator #(.width(3)) comparator_19 (.a(Instruction[14:12]), .b(3'b101), .eq(comparator_19_eq));  // open: gt, lt
  Comparator #(.width(7)) comparator_20 (.a(Instruction[31:25]), .b({7{1'b0}}), .eq(comparator_20_eq));  // open: gt, lt
  Comparator #(.width(7)) comparator_21 (
    .a(Instruction[31:25]), .b(7'b0000001), .eq(comparator_21_eq));  // open: gt, lt
  Comparator #(.width(7)) comparator_22 (
    .a(Instruction[31:25]), .b(7'b0100000), .eq(comparator_22_eq));  // open: gt, lt
  Comparator #(.width(7)) comparator_23 (.a(Instruction[31:25]), .b({7{1'b0}}), .eq(comparator_23_eq));  // open: gt, lt
  Comparator #(.width(7)) comparator_24 (
    .a(Instruction[31:25]), .b(7'b0000001), .eq(comparator_24_eq));  // open: gt, lt
  Comparator #(.width(7)) comparator_25 (
    .a(Instruction[31:25]), .b(7'b0000001), .eq(comparator_25_eq));  // open: gt, lt
  Comparator #(.width(7)) comparator_26 (.a(Instruction[31:25]), .b({7{1'b0}}), .eq(comparator_26_eq));  // open: gt, lt
  Comparator #(.width(7)) comparator_27 (.a(Instruction[31:25]), .b({7{1'b0}}), .eq(comparator_27_eq));  // open: gt, lt
  Comparator #(.width(7)) comparator_28 (.a(Instruction[31:25]), .b({7{1'b0}}), .eq(comparator_28_eq));  // open: gt, lt
  Comparator #(.width(7)) comparator_29 (
    .a(Instruction[31:25]), .b(7'b0100000), .eq(comparator_29_eq));  // open: gt, lt
  Comparator #(.width(7)) comparator_30 (.a(Instruction[31:25]), .b({7{1'b0}}), .eq(comparator_30_eq));  // open: gt, lt
  Comparator #(.width(7)) comparator_31 (.a(Instruction[31:25]), .b({7{1'b0}}), .eq(comparator_31_eq));  // open: gt, lt
  and and_9 (is_add, comparator_14_eq, is_Rtype, comparator_20_eq);
  and and_10 (is_sll, comparator_15_eq, is_Rtype, comparator_23_eq);
  and and_11 (is_mulh, comparator_15_eq, is_Rtype, comparator_24_eq);
  and and_12 (is_mulhu, comparator_16_eq, is_Rtype, comparator_25_eq);
  and and_13 (is_slt, comparator_17_eq, is_Rtype, comparator_26_eq);
  and and_14 (is_xor, comparator_18_eq, is_Rtype, comparator_27_eq);
  and and_15 (is_srl, comparator_19_eq, is_Rtype, comparator_28_eq);
  and and_16 (is_sra, comparator_19_eq, is_Rtype, comparator_29_eq);
  and and_17 (is_or, comparator_12_eq, is_Rtype, comparator_30_eq);
  and and_18 (is_and, comparator_13_eq, is_Rtype, comparator_31_eq);
  and and_19 (is_mul, comparator_14_eq, is_Rtype, comparator_21_eq);
  and and_20 (is_sub, comparator_14_eq, is_Rtype, comparator_22_eq);

  assign PCSel = 1'b0;

  // Other names for the same wires on the sheet: opcode[6:0] = Instruction[6:0]; fun3[2:0] = Instruction[14:12];
  //   fun7[6:0] = Instruction[31:25]

  // Notes on the sheet:
  //   INPUTS to your circuit
  //   Connect ROM Input here ->
  //   contents of rom_1 (hex, n*v repeats v):
  //   100f 140f 160f 108f 148f 158f 110f 120f 128f 168f 130f 138f 0 0 0 1041 10c1 1141 1241 12c1 16c1 1341
  //   13c1
  //   ROM FOR CONTROL LOGIC
  //   DON'T CHANGE THE LOCATIONS OF THE INPUTS AND OUTPUTS!
  //   This is only if you choose to do the ROM option
  //   CONNECT
  //   WIRE
  //   TO
  //   USE
  //   ROM
  //   OUTPUT from your circuit
  //   Reminder: If using ROM, use combinational logic for PCSel
endmodule
